// Logisim project control-logic.circ as structural Verilog: 4 circuits, main circuit control_logic
module control_logic (
  input  [31:0] Instruction,
  input  BrEq,
  input  BrLt,
  output PCSel,
  output RegWEn,
  output [2:0] ImmSel,
  output BrUn,
  output ASel,
  output BSel,
  output [3:0] ALUSel,
  output MemWEn,
  output [1:0] WBSel
);

  wire Auipc, b_type_pcsel_1_pcsel, Bformat, Iformat, Jalr, JFormat, Load, Lui, MemWEN_t, not_1_out,
       not_2_out, not_3_out, not_4_out, not_5_out, not_6_out, not_7_out, not_8_out, not_9_out, not_10_out,
       not_11_out, not_12_out, not_13_out, not_14_out, not_15_out, not_16_out, not_17_out, not_18_out,
       not_19_out, not_20_out, not_21_out, not_22_out, not_23_out, not_24_out, not_25_out, not_26_out,
       not_27_out, not_28_out, not_29_out, not_30_out, not_31_out, not_32_out, not_33_out, not_34_out,
       not_35_out, not_36_out, not_37_out, not_38_out, not_39_out, not_40_out, Rformat, Store, undriven;
  wire [1:0] undriven_3;
  wire [2:0] undriven_2;
  wire [3:0] i_type_func3_handler_1_alusel, Instruction_Type, r_type_alusel_handler_1_alusel;
  wire [15:0] rom_1_data;

  not not_1 (not_1_out, Instruction[2]);
  not not_2 (not_2_out, Instruction[2]);
  not not_3 (not_3_out, Instruction[6]);
  not not_4 (not_4_out, Instruction[2]);
  not not_5 (not_5_out, Instruction[6]);
  not not_6 (not_6_out, Instruction[2]);
  not not_7 (not_7_out, Instruction[3]);
  not not_8 (not_8_out, Instruction[5]);
  not not_9 (not_9_out, Instruction[6]);
  not not_10 (not_10_out, Instruction[2]);
  not not_11 (not_11_out, Instruction[3]);
  not not_12 (not_12_out, Instruction[6]);
  not not_13 (not_13_out, Instruction[3]);
  not not_14 (not_14_out, Instruction[4]);
  not not_15 (not_15_out, Instruction[3]);
  not not_16 (not_16_out, Instruction[4]);
  not not_17 (not_17_out, Instruction[5]);
  not not_18 (not_18_out, Instruction[3]);
  not not_19 (not_19_out, Instruction[4]);
  not not_20 (not_20_out, Instruction[4]);
  not not_21 (not_21_out, Instruction[3]);
  not not_22 (not_22_out, Instruction[4]);
  not not_23 (not_23_out, Instruction[3]);
  not not_24 (not_24_out, Instruction[5]);
  not not_25 (not_25_out, Instruction[6]);
  not not_26 (not_26_out, Instruction[3]);
  not not_27 (not_27_out, Instruction[6]);
  and and_1 (Iformat, not_6_out, not_7_out, Instruction[4], not_8_out, not_9_out);
  and and_2 (Rformat, not_10_out, not_11_out, Instruction[4], Instruction[5], not_12_out);
  and and_3 (Bformat, not_1_out, not_13_out, not_14_out, Instruction[5], Instruction[6]);
  and and_4 (Load, not_2_out, not_15_out, not_16_out, not_17_out, not_3_out);
  and and_5 (Store, not_4_out, not_18_out, not_19_out, Instruction[5], not_5_out);
  and and_6 (JFormat, Instruction[2], Instruction[3], not_20_out, Instruction[5], Instruction[6]);
  and and_7 (Jalr, Instruction[2], not_21_out, not_22_out, Instruction[5], Instruction[6]);
  and and_8 (Auipc, Instruction[2], not_23_out, Instruction[4], not_24_out, not_25_out);
  and and_9 (Lui, Instruction[2], not_26_out, Instruction[4], Instruction[5], not_27_out);
  Priority_Encoder #(.disabled("Z"), .select_enc(4)) priority_encoder_1 (
    .in0(Iformat), .in1(Rformat), .in2(Bformat), .in3(Load), .in4(Store), .in5(JFormat), .in6(Jalr),
    .in7(Auipc), .in8(Lui), .out(Instruction_Type));  // open: in9, in10, in11, in12, in13, in14, in15, gs, en_out, en_in
  I_Type_func3_handler i_type_func3_handler_1 (
    .func3(Instruction[14:12]), .func7_bit30(Instruction[30]), .ALUSel(i_type_func3_handler_1_alusel));
  R_Type_ALUSel_Handler r_type_alusel_handler_1 (
    .func3(Instruction[14:12]), .func7(Instruction[31:25]), .ALUSel(r_type_alusel_handler_1_alusel));
  not not_28 (not_28_out, Load);
  not not_29 (not_29_out, JFormat);
  not not_30 (not_30_out, Jalr);
  not not_31 (not_31_out, Auipc);
  not not_32 (not_32_out, Lui);
  Multiplexer #(.select(4), .width(4)) multiplexer_1 (
    .in0(i_type_func3_handler_1_alusel), .in1(r_type_alusel_handler_1_alusel), .in2(4'b0000), .in3(4'b0000),
    .in4(4'b0000), .in5(4'b0000), .in6(4'b0000), .in7(4'b0000), .in8(4'b1111), .out(ALUSel),
    .sel(Instruction_Type));  // open: in9, in10, in11, in12, in13, in14, in15
  not not_33 (not_33_out, Bformat);
  not not_34 (not_34_out, Store);
  not not_35 (not_35_out, Iformat);
  not not_36 (not_36_out, Rformat);
  not not_37 (not_37_out, Bformat);
  not not_38 (not_38_out, Iformat);
  not not_39 (not_39_out, Rformat);
  not not_40 (not_40_out, Rformat);
  Multiplexer #(.select(4), .width(3)) multiplexer_2 (
    .in0(3'b000), .in1(undriven_2), .in2(3'b010), .in3(3'b000), .in4(3'b001), .in5(3'b100), .in6(3'b000),
    .in7(3'b011), .in8(3'b011), .out(ImmSel), .sel(Instruction_Type));  // open: in9, in10, in11, in12, in13, in14, in15
  Multiplexer #(.select(4)) multiplexer_3 (
    .in0(Iformat), .in1(Rformat), .in2(not_33_out), .in3(Load), .in4(not_34_out), .in5(JFormat), .in6(Jalr),
    .in7(Auipc), .in8(Lui), .out(RegWEn), .sel(Instruction_Type));  // open: in9, in10, in11, in12, in13, in14, in15
  Multiplexer #(.select(4)) multiplexer_4 (
    .in0(not_35_out), .in1(not_36_out), .in2(not_37_out), .in3(not_28_out), .in4(Store), .in5(not_29_out),
    .in6(not_30_out), .in7(not_31_out), .in8(not_32_out), .out(MemWEN_t), .sel(Instruction_Type));  // open: in9, in10, in11, in12, in13, in14, in15
  Multiplexer #(.select(4)) multiplexer_5 (
    .in0(not_38_out), .in1(not_39_out), .in2(Bformat), .in3(1'b0), .in4(1'b0), .in5(1'b1), .in6(1'b0),
    .in7(1'b1), .in8(undriven), .out(ASel), .sel(Instruction_Type));  // open: in9, in10, in11, in12, in13, in14, in15
  Multiplexer #(.select(4)) multiplexer_6 (
    .in0(Iformat), .in1(not_40_out), .in2(Bformat), .in3(1'b1), .in4(1'b1), .in5(1'b1), .in6(1'b1),
    .in7(1'b1), .in8(1'b1), .out(BSel), .sel(Instruction_Type));  // open: in9, in10, in11, in12, in13, in14, in15
  Multiplexer #(.select(4), .width(2)) multiplexer_7 (
    .in0(2'b01), .in1(2'b01), .in2(undriven_3), .in3(2'b00), .in4(undriven_3), .in5(2'b10), .in6(2'b10),
    .in7(2'b01), .in8(2'b01), .out(WBSel), .sel(Instruction_Type));  // open: in9, in10, in11, in12, in13, in14, in15
  B_Type_PCSel b_type_pcsel_1 (.BrLt(BrLt), .BrEq(BrEq), .Func3(Instruction[14:12]), .PCSel(b_type_pcsel_1_pcsel));
  Multiplexer #(.select(4)) multiplexer_8 (
    .in0(1'b0), .in1(1'b0), .in2(b_type_pcsel_1_pcsel), .in3(1'b0), .in4(1'b0), .in5(1'b1), .in6(1'b1),
    .in7(1'b0), .in8(1'b0), .out(PCSel), .sel(Instruction_Type));  // open: in9, in10, in11, in12, in13, in14, in15
  ROM #(.addrWidth(6), .dataWidth(16)) rom_1 (.data(rom_1_data));  // open: addr

  assign BrUn = Instruction[13];

  // Other names for the same wires on the sheet: Func3[2:0] = Instruction[14:12]; opcode[4:0] = Instruction[6:2]

  // Notes on the sheet:
  //   INPUTS to your circuit
  //   We only consider RV32 here so the 0 bit and 1 bit of instructions are not considered since they are all the same 
  //   Determine Instruction type 
  //   0: for I-type
  //   DON'T CHANGE THE LOCATIONS OF THE INPUTS AND OUTPUTS!
  //   OUTPUT from your circuit
  //   BrUn
  //   PCSel
  //   RegWEN
  //   MemRW
  //   ASel
  //   BSel
  //   WBSel
  //   ImmSel
  //   ALUSel
  //   Connect ROM Input here ->
  //   ROM FOR CONTROL LOGIC
  //   This is only if you choose to do the ROM option
  //   CONNECT
  //   WIRE
  //   TO
  //   USE
  //   ROM
  //   Reminder: If using ROM, use combinational logic for PCSel
endmodule

module I_Type_func3_handler (
  input  [2:0] func3,
  input  func7_bit30,
  output [3:0] ALUSel
);

  wire and_1_out, not_1_out;
  wire [3:0] bit_extender_1_out;

  not not_1 (not_1_out, func3[1]);
  assign bit_extender_1_out = {{1{1'b0}}, func3};  // Bit_Extender bit_extender_1
  and and_1 (and_1_out, func3[0], not_1_out, func3[2], func7_bit30);
  Multiplexer #(.width(4)) multiplexer_1 (.in0(bit_extender_1_out), .in1(4'b1101), .out(ALUSel), .sel(and_1_out));

  // Notes on the sheet:
  //   If it is srai
endmodule

module R_Type_ALUSel_Handler (
  input  [2:0] func3,
  input  [6:0] func7,
  output [3:0] ALUSel
);

  wire [3:0] bit_extender_1_out, multiplexer_1_out, multiplexer_2_out;

  Multiplexer #(.select(2), .width(4)) multiplexer_1 (
    .in0(4'b1000), .in1(4'b1001), .in3(4'b1011), .out(multiplexer_1_out), .sel(func3[1:0]));  // open: in2
  Multiplexer #(.width(4)) multiplexer_2 (.in0(4'b1100), .in1(4'b1101), .out(multiplexer_2_out), .sel(func3[0]));
  assign bit_extender_1_out = {{1{1'b0}}, func3};  // Bit_Extender bit_extender_1
  Multiplexer #(.select(2), .width(4)) multiplexer_3 (
    .in0(bit_extender_1_out), .in1(multiplexer_1_out), .in2(multiplexer_2_out), .out(ALUSel),
    .sel({func7[5], func7[0]}));  // open: in3

  // Notes on the sheet:
  //   mul
  //   mulh
  //   mulhu
  //   sub
  //   sra
endmodule

module B_Type_PCSel (
  input  BrLt,
  input  BrEq,
  input  [2:0] Func3,
  output PCSel
);

  wire and_1_out, not_1_out, not_2_out, xor_1_out, xor_2_out;

  xor xor_1 (xor_1_out, BrEq, Func3[0]);
  xor xor_2 (xor_2_out, BrLt, Func3[0]);
  not not_1 (not_1_out, Func3[1]);
  not not_2 (not_2_out, Func3[2]);
  and and_1 (and_1_out, not_1_out, not_2_out);
  Multiplexer multiplexer_1 (.in0(xor_2_out), .in1(xor_1_out), .out(PCSel), .sel(and_1_out));

  // Other names for the same wires on the sheet: Func3_12 = Func3[0]; Func3_13 = Func3[1]; Func3_14 = Func3[2]
endmodule
