// Logisim project cpu.circ as structural Verilog: 1 circuit, main circuit cpu
module cpu (
  input  clk,
  input  [31:0] Instruction,
  input  [31:0] MemReadData,
  output [31:0] MemAddress,
  output [31:0] ProgramCounter,
  output [31:0] ra,
  output [31:0] sp,
  output [31:0] t0,
  output [31:0] t1,
  output [31:0] t2,
  output [31:0] s0,
  output [31:0] s1,
  output [31:0] a0,
  output [3:0] MemWriteMask,
  output [31:0] MemWriteData
);

  wire ASel, BrEq, BrLt, BrUn, BSel, MemWEn, PCSel, RegWEn;
  wire [1:0] WBSel;
  wire [2:0] ImmSel;
  wire [3:0] ALUSel;
  wire [4:0] ReadIndex1, ReadIndex2;
  wire [31:0] Imm, MemToReg, multiplexer_1_out, multiplexer_2_out, multiplexer_3_out, multiplexer_4_out,
       PC_Next, ReadDataA, ReadDataB, Stage2_Instruction, Stage2_PC_Next, Stage2_ProgramCounter, WriteData;

  Adder #(.width(32)) adder_1 (.a(ProgramCounter), .b(32'h4), .out(PC_Next));  // open: cin, cout
  Register #(.width(32)) PC (.D(multiplexer_1_out), .clk(clk), .Q(ProgramCounter));  // open: en, clr
  Multiplexer #(.width(32)) multiplexer_1 (.in0(PC_Next), .in1(MemAddress), .out(multiplexer_1_out), .sel(PCSel));
  Register #(.width(32)) register_1 (
    .D(multiplexer_2_out), .clk(clk),
    .Q({Stage2_Instruction[31:25], ReadIndex2, ReadIndex1, Stage2_Instruction[14:0]}));  // open: en, clr
  Multiplexer #(.width(32)) multiplexer_2 (.in0(Instruction), .in1(32'h13), .out(multiplexer_2_out), .sel(PCSel));
  Register #(.width(32)) register_2 (.D(ProgramCounter), .clk(clk), .Q(Stage2_ProgramCounter));  // open: en, clr
  Register #(.width(32)) register_3 (.D(PC_Next), .clk(clk), .Q(Stage2_PC_Next));  // open: en, clr
  control_logic control_logic_1 (
    .Instruction({Stage2_Instruction[31:25], ReadIndex2, ReadIndex1, Stage2_Instruction[14:0]}), .BrEq(BrEq),
    .BrLt(BrLt), .PCSel(PCSel), .RegWEn(RegWEn), .ImmSel(ImmSel), .BrUn(BrUn), .ASel(ASel), .BSel(BSel),
    .ALUSel(ALUSel), .MemWEn(MemWEn), .WBSel(WBSel));
  regfile regfile_1 (
    .ReadIndex1(ReadIndex1), .ReadIndex2(ReadIndex2), .WriteIndex(Stage2_Instruction[11:7]),
    .WriteData(WriteData), .RegWEn(RegWEn), .clk(clk), .ra(ra), .sp(sp), .t0(t0), .t1(t1), .t2(t2), .s0(s0),
    .s1(s1), .a0(a0), .ReadData1(ReadDataA), .ReadData2(ReadDataB));
  imm_gen imm_gen_1 (
    .Instruction({Stage2_Instruction[31:25], ReadIndex2, ReadIndex1, Stage2_Instruction[14:0]}),
    .ImmSel(ImmSel), .Immediate(Imm));
  Multiplexer #(.width(32)) multiplexer_3 (
    .in0(ReadDataA), .in1(Stage2_ProgramCounter), .out(multiplexer_3_out), .sel(ASel));
  Multiplexer #(.width(32)) multiplexer_4 (.in0(ReadDataB), .in1(Imm), .out(multiplexer_4_out), .sel(BSel));
  branch_comp branch_comp_1 (.BrData1(ReadDataA), .BrData2(ReadDataB), .BrUn(BrUn), .BrEq(BrEq), .BrLt(BrLt));
  alu alu_1 (.A(multiplexer_3_out), .B(multiplexer_4_out), .ALUSel(ALUSel), .ALUResult(MemAddress));
  Multiplexer #(.select(2), .width(32)) multiplexer_5 (
    .in0(MemToReg), .in1(MemAddress), .in2(Stage2_PC_Next), .out(WriteData), .sel(WBSel));  // open: in3
  partial_store partial_store_1 (
    .Instruction({Stage2_Instruction[31:25], ReadIndex2, ReadIndex1, Stage2_Instruction[14:0]}),
    .MemAddress(MemAddress), .DataFromReg(ReadDataB), .MemWEn(MemWEn), .MemWriteMask(MemWriteMask),
    .DataToMem(MemWriteData));
  partial_load partial_load_1 (
    .Instruction({Stage2_Instruction[31:25], ReadIndex2, ReadIndex1, Stage2_Instruction[14:0]}),
    .MemAddress(MemAddress), .DataFromMem(MemReadData), .DataToReg(MemToReg));

  // Other names for the same wires on the sheet: ALUResult[31:0] = MemAddress;
  //   WriteIndex[4:0] = Stage2_Instruction[11:7]; Stage2_Instruction[24:15] = {ReadIndex2, ReadIndex1}

  // Notes on the sheet:
  //   If Jump or Branch
  //   skip pc+4
  //   To IMEM
  //   IMEM (do **NOT** move this)
  //   From IMEM
  //   Inputs/Outputs for testing. Do **NOT** move these.
  //   It is OK to move the PC, RegFile, ALU, MEM, Branch Comp, Imm Gen, Partial Load, Partial Store and Control Logic to wherever is most convenient for you when constructing your CPU, and to delete this text
  //   To DMEM
  //   DMEM (do **NOT** move this)
  //   From DMEM
endmodule
