// Logisim project partial-store.circ as structural Verilog: 1 circuit, main circuit partial_store
module partial_store (
  input  [31:0] Instruction,
  input  [31:0] MemAddress,
  input  [31:0] DataFromReg,
  input  MemWEn,
  output [3:0] MemWriteMask,
  output [31:0] DataToMem
);

  wire [3:0] multiplexer_4_out, sb, sh;
  wire [31:0] sb_data, sh_data;

  Multiplexer #(.select(2), .width(32)) multiplexer_1 (
    .in0(sb_data), .in1(sh_data), .in2(DataFromReg), .out(DataToMem), .sel(Instruction[13:12]));  // open: in3
  Multiplexer #(.width(32)) multiplexer_2 (
    .in0({{16{1'b0}}, DataFromReg[15:0]}), .in1({DataFromReg[15:0], {16{1'b0}}}), .out(sh_data),
    .sel(MemAddress[1]));
  Multiplexer #(.width(4)) multiplexer_3 (.in0(4'b0000), .in1(multiplexer_4_out), .out(MemWriteMask), .sel(MemWEn));
  Multiplexer #(.select(2), .width(4)) multiplexer_4 (
    .in0(sb), .in1(sh), .in2(4'b1111), .out(multiplexer_4_out), .sel(Instruction[13:12]));  // open: in3
  Multiplexer #(.select(2), .width(4)) multiplexer_5 (
    .in0(4'b0001), .in1(4'b0010), .in2(4'b0100), .in3(4'b1000), .out(sb), .sel(MemAddress[1:0]));
  Multiplexer #(.width(4)) multiplexer_6 (.in0(4'b0011), .in1(4'b1100), .out(sh), .sel(MemAddress[1]));
  Multiplexer #(.select(2), .width(32)) multiplexer_7 (
    .in0({{24{1'b0}}, DataFromReg[7:0]}), .in1({{16{1'b0}}, DataFromReg[7:0], {8{1'b0}}}),
    .in2({{8{1'b0}}, DataFromReg[7:0], {16{1'b0}}}), .in3({DataFromReg[7:0], {24{1'b0}}}), .out(sb_data),
    .sel(MemAddress[1:0]));

  // Other names for the same wires on the sheet: Bottom_8_bits[7:0] = DataFromReg[7:0];
  //   Bottom_16_bits[15:0] = DataFromReg[15:0]

  // Notes on the sheet:
  //   INPUTS to your circuit
  //   DON'T CHANGE THE LOCATIONS OF THE INPUTS AND OUTPUTS!
  //   OUTPUT from your circuit
endmodule
