// Logisim project regfile.circ as structural Verilog: 1 circuit, main circuit regfile
module regfile (
  input  [4:0] ReadIndex1,
  input  [4:0] ReadIndex2,
  input  [4:0] WriteIndex,
  input  [31:0] WriteData,
  input  RegWEn,
  input  clk,
  output [31:0] ra,
  output [31:0] sp,
  output [31:0] t0,
  output [31:0] t1,
  output [31:0] t2,
  output [31:0] s0,
  output [31:0] s1,
  output [31:0] a0,
  output [31:0] ReadData1,
  output [31:0] ReadData2
);

  wire and_1_out, and_2_out, and_3_out, and_4_out, and_5_out, and_6_out, and_7_out, and_8_out, and_9_out,
       and_10_out, and_11_out, and_12_out, and_13_out, and_14_out, and_15_out, and_16_out, and_17_out,
       and_18_out, and_19_out, and_20_out, and_21_out, and_22_out, and_23_out, and_24_out, and_25_out,
       and_26_out, and_27_out, and_28_out, and_29_out, and_30_out, and_31_out, demultiplexer_1_out0,
       WriteSel1, WriteSel2, WriteSel3, WriteSel4, WriteSel5, WriteSel6, WriteSel7, WriteSel8, WriteSel9,
       WriteSel10, WriteSel11, WriteSel12, WriteSel13, WriteSel14, WriteSel15, WriteSel16, WriteSel17,
       WriteSel18, WriteSel19, WriteSel20, WriteSel21, WriteSel22, WriteSel23, WriteSel24, WriteSel25,
       WriteSel26, WriteSel27, WriteSel28, WriteSel29, WriteSel30, WriteSel31;
  wire [31:0] x3, x4, x11, x12, x13, x14, x15, x16, x17, x18, x19, x20, x21, x22, x23, x24, x25, x26, x27,
       x28, x29, x30, x31;

  and and_1 (and_1_out, WriteSel4, RegWEn);
  and and_2 (and_2_out, WriteSel5, RegWEn);
  and and_3 (and_3_out, WriteSel7, RegWEn);
  and and_4 (and_4_out, WriteSel10, RegWEn);
  and and_5 (and_5_out, WriteSel11, RegWEn);
  and and_6 (and_6_out, WriteSel14, RegWEn);
  Register #(.width(32)) register_1 (.D(WriteData), .en(and_7_out), .clk(clk), .Q(ra));  // open: clr
  and and_7 (and_7_out, WriteSel1, RegWEn);
  Register #(.width(32)) register_2 (.D(WriteData), .en(and_8_out), .clk(clk), .Q(sp));  // open: clr
  and and_8 (and_8_out, WriteSel2, RegWEn);
  Register #(.width(32)) register_3 (.D(WriteData), .en(and_9_out), .clk(clk), .Q(x3));  // open: clr
  and and_9 (and_9_out, WriteSel3, RegWEn);
  Register #(.width(32)) register_4 (.D(WriteData), .en(and_1_out), .clk(clk), .Q(x4));  // open: clr
  Register #(.width(32)) register_5 (.D(WriteData), .en(and_2_out), .clk(clk), .Q(t0));  // open: clr
  Register #(.width(32)) register_6 (.D(WriteData), .en(and_10_out), .clk(clk), .Q(t1));  // open: clr
  and and_10 (and_10_out, WriteSel6, RegWEn);
  Register #(.width(32)) register_7 (.D(WriteData), .en(and_3_out), .clk(clk), .Q(t2));  // open: clr
  Register #(.width(32)) register_8 (.D(WriteData), .en(and_11_out), .clk(clk), .Q(s0));  // open: clr
  and and_11 (and_11_out, WriteSel8, RegWEn);
  Register #(.width(32)) register_9 (.D(WriteData), .en(and_12_out), .clk(clk), .Q(s1));  // open: clr
  and and_12 (and_12_out, WriteSel9, RegWEn);
  Register #(.width(32)) register_10 (.D(WriteData), .en(and_4_out), .clk(clk), .Q(a0));  // open: clr
  Register #(.width(32)) register_11 (.D(WriteData), .en(and_5_out), .clk(clk), .Q(x11));  // open: clr
  Register #(.width(32)) register_12 (.D(WriteData), .en(and_13_out), .clk(clk), .Q(x12));  // open: clr
  and and_13 (and_13_out, WriteSel12, RegWEn);
  Register #(.width(32)) register_13 (.D(WriteData), .en(and_14_out), .clk(clk), .Q(x13));  // open: clr
  and and_14 (and_14_out, WriteSel13, RegWEn);
  Register #(.width(32)) register_14 (.D(WriteData), .en(and_6_out), .clk(clk), .Q(x14));  // open: clr
  Register #(.width(32)) register_15 (.D(WriteData), .en(and_15_out), .clk(clk), .Q(x15));  // open: clr
  and and_15 (and_15_out, WriteSel15, RegWEn);
  Register #(.width(32)) register_16 (.D(WriteData), .en(and_16_out), .clk(clk), .Q(x16));  // open: clr
  and and_16 (and_16_out, WriteSel16, RegWEn);
  Register #(.width(32)) register_17 (.D(WriteData), .en(and_17_out), .clk(clk), .Q(x17));  // open: clr
  and and_17 (and_17_out, WriteSel17, RegWEn);
  and and_18 (and_18_out, WriteSel18, RegWEn);
  and and_19 (and_19_out, WriteSel19, RegWEn);
  Register #(.width(32)) register_18 (.D(WriteData), .en(and_20_out), .clk(clk), .Q(x20));  // open: clr
  and and_20 (and_20_out, WriteSel20, RegWEn);
  Register #(.width(32)) register_19 (.D(WriteData), .en(and_21_out), .clk(clk), .Q(x21));  // open: clr
  and and_21 (and_21_out, WriteSel21, RegWEn);
  Register #(.width(32)) register_20 (.D(WriteData), .en(and_22_out), .clk(clk), .Q(x22));  // open: clr
  and and_22 (and_22_out, WriteSel22, RegWEn);
  Register #(.width(32)) register_21 (.D(WriteData), .en(and_23_out), .clk(clk), .Q(x23));  // open: clr
  and and_23 (and_23_out, WriteSel23, RegWEn);
  Register #(.width(32)) register_22 (.D(WriteData), .en(and_24_out), .clk(clk), .Q(x24));  // open: clr
  and and_24 (and_24_out, WriteSel24, RegWEn);
  Register #(.width(32)) register_23 (.D(WriteData), .en(and_25_out), .clk(clk), .Q(x25));  // open: clr
  and and_25 (and_25_out, WriteSel25, RegWEn);
  and and_26 (and_26_out, WriteSel26, RegWEn);
  and and_27 (and_27_out, WriteSel27, RegWEn);
  and and_28 (and_28_out, WriteSel28, RegWEn);
  and and_29 (and_29_out, WriteSel29, RegWEn);
  and and_30 (and_30_out, WriteSel30, RegWEn);
  and and_31 (and_31_out, WriteSel31, RegWEn);
  Register #(.width(32)) register_24 (.D(WriteData), .en(and_18_out), .clk(clk), .Q(x18));  // open: clr
  Register #(.width(32)) register_25 (.D(WriteData), .en(and_19_out), .clk(clk), .Q(x19));  // open: clr
  Register #(.width(32)) register_26 (.D(WriteData), .en(and_26_out), .clk(clk), .Q(x26));  // open: clr
  Register #(.width(32)) register_27 (.D(WriteData), .en(and_27_out), .clk(clk), .Q(x27));  // open: clr
  Register #(.width(32)) register_28 (.D(WriteData), .en(and_28_out), .clk(clk), .Q(x28));  // open: clr
  Register #(.width(32)) register_29 (.D(WriteData), .en(and_29_out), .clk(clk), .Q(x29));  // open: clr
  Register #(.width(32)) register_30 (.D(WriteData), .en(and_30_out), .clk(clk), .Q(x30));  // open: clr
  Register #(.width(32)) register_31 (.D(WriteData), .en(and_31_out), .clk(clk), .Q(x31));  // open: clr
  Demultiplexer #(.select(5)) demultiplexer_1 (
    .out0(demultiplexer_1_out0), .out1(WriteSel1), .out2(WriteSel2), .out3(WriteSel3), .out4(WriteSel4),
    .out5(WriteSel5), .out6(WriteSel6), .out7(WriteSel7), .out8(WriteSel8), .out9(WriteSel9),
    .out10(WriteSel10), .out11(WriteSel11), .out12(WriteSel12), .out13(WriteSel13), .out14(WriteSel14),
    .out15(WriteSel15), .out16(WriteSel16), .out17(WriteSel17), .out18(WriteSel18), .out19(WriteSel19),
    .out20(WriteSel20), .out21(WriteSel21), .out22(WriteSel22), .out23(WriteSel23), .out24(WriteSel24),
    .out25(WriteSel25), .out26(WriteSel26), .out27(WriteSel27), .out28(WriteSel28), .out29(WriteSel29),
    .out30(WriteSel30), .out31(WriteSel31), .in(1'b1), .sel(WriteIndex));
  Multiplexer #(.select(5), .width(32)) multiplexer_1 (
    .in0({32{1'b0}}), .in1(ra), .in2(sp), .in3(x3), .in4(x4), .in5(t0), .in6(t1), .in7(t2), .in8(s0),
    .in9(s1), .in10(a0), .in11(x11), .in12(x12), .in13(x13), .in14(x14), .in15(x15), .in16(x16), .in17(x17),
    .in18(x18), .in19(x19), .in20(x20), .in21(x21), .in22(x22), .in23(x23), .in24(x24), .in25(x25),
    .in26(x26), .in27(x27), .in28(x28), .in29(x29), .in30(x30), .in31(x31), .out(ReadData1), .sel(ReadIndex1));
  Multiplexer #(.select(5), .width(32)) multiplexer_2 (
    .in0({32{1'b0}}), .in1(ra), .in2(sp), .in3(x3), .in4(x4), .in5(t0), .in6(t1), .in7(t2), .in8(s0),
    .in9(s1), .in10(a0), .in11(x11), .in12(x12), .in13(x13), .in14(x14), .in15(x15), .in16(x16), .in17(x17),
    .in18(x18), .in19(x19), .in20(x20), .in21(x21), .in22(x22), .in23(x23), .in24(x24), .in25(x25),
    .in26(x26), .in27(x27), .in28(x28), .in29(x29), .in30(x30), .in31(x31), .out(ReadData2), .sel(ReadIndex2));

  // Other names for the same wires on the sheet: x1[31:0] = ra; x2[31:0] = sp; x5[31:0] = t0; x6[31:0] = t1;
  //   x7[31:0] = t2; x8[31:0] = s0; x9[31:0] = s1; x10[31:0] = a0

  // Notes on the sheet:
  //   INPUTS to your circuit
  //   DON'T CHANGE THE LOCATIONS OF THE INPUTS AND OUTPUTS!
  //   These are DEBUG/TEST outputs from your circuit.
  //   OUTPUTS from your circuit
endmodule
